// Logisim project alu2.circ as structural Verilog: 2 circuits, main circuit main
module main (
  input  [3:0] in_1,
  input  C_in,
  input  [15:0] A,
  input  [15:0] B,
  output V,
  output N,
  output [15:0] out_7,
  output C_out,
  output Z
);

  wire adder_1_cout, comparator_1_eq, subtractor_1_bout;
  wire [15:0] adder_1_out, and_1_out, divider_1_out, multiplier_1_out, negator_1_out, not_1_out, or_1_out,
       subtractor_1_out, xor_1_out;

  Multiplier #(.width(16)) multiplier_1 (.a(A), .b(B), .out(multiplier_1_out));  // open: cin, cout
  Adder #(.width(16)) adder_1 (.a(A), .b(B), .out(adder_1_out), .cin(C_in), .cout(adder_1_cout));
  Divider #(.width(16)) divider_1 (.a(A), .b(B), .out(divider_1_out));  // open: upper, rem
  assign and_1_out = A & B;  // AND_Gate and_1, 16 bits wide
  assign or_1_out = A | B;  // OR_Gate or_1, 16 bits wide
  assign xor_1_out = A ^ B;  // XOR_Gate xor_1, 16 bits wide
  Subtractor #(.width(16)) subtractor_1 (.a(A), .b(B), .out(subtractor_1_out), .bin(C_in), .bout(subtractor_1_bout));
  assign not_1_out = ~A;  // NOT_Gate not_1, 16 bits wide
  Negator #(.width(16)) negator_1 (.in(A), .out(negator_1_out));
  Comparator #(.width(16)) comparator_1 (.a(A), .b(B), .eq(comparator_1_eq));  // open: gt, lt
  Multiplexer #(.select(4), .width(16)) multiplexer_1 (
    .in0(adder_1_out), .in1(subtractor_1_out), .in2(multiplier_1_out), .in3(divider_1_out), .in4(and_1_out),
    .in5(or_1_out), .in6(not_1_out), .in7(xor_1_out), .in13(negator_1_out), .out({N, out_7[14:0]}), .sel(in_1));  // open: in8, in9, in10, in11, in12, in14, in15
  Multiplexer #(.select(4)) multiplexer_2 (
    .in0(adder_1_cout), .in1(subtractor_1_bout), .out(C_out), .sel(in_1));  // open: in2, in3, in4, in5, in6, in7, in8, in9, in10, in11, in12, in13, in14, in15
  oveflow oveflow_1 (.a(A[15]), .b(B[15]), .r(N), .v(V));
  Pull_Resistor pull_resistor_1 (.node(C_out));
  nor nor_1 (Z, out_7[0], out_7[1], out_7[2], out_7[3], out_7[4], out_7[5], out_7[6], out_7[7], out_7[8], out_7[9], out_7[10], out_7[11], out_7[12], out_7[13], out_7[14], N);

  assign out_7[15] = N;
endmodule

module oveflow (
  input  a,
  input  b,
  input  r,
  output v
);

  wire and_1_out, and_2_out, and_3_out, and_4_out, not_1_out, not_2_out, not_3_out;

  not not_1 (not_1_out, a);
  not not_2 (not_2_out, b);
  and and_1 (and_1_out, not_1_out, not_2_out);
  and and_2 (and_2_out, a, b);
  not not_3 (not_3_out, r);
  and and_3 (and_3_out, and_1_out, r);
  and and_4 (and_4_out, and_2_out, not_3_out);
  or or_1 (v, and_3_out, and_4_out);
endmodule
