// Logisim project clock1.circ as structural Verilog: 1 circuit, main circuit main
module main (
  input  [5:0] in_1,
  input  [5:0] in_2
);

  wire clock_1_out;
  wire [3:0] divider_2_out;
  wire [5:0] counter_1_q, divider_1_out, divider_1_rem, divider_2_rem, sec_q;
  wire [5:4] divider_2_out_2;

  Clock clock_1 (.out(clock_1_out));
  Counter #(.width(6), .max('h3f)) sec (.Q(sec_q), .clk(clock_1_out));  // open: load, D, count, carry, clr
  Divider #(.width(6)) divider_1 (.a(sec_q), .b(in_2), .out(divider_1_out), .rem(divider_1_rem));  // open: upper
  // Probe on divider_1_out
  // Probe on divider_2_rem
  Counter #(.width(6), .max('h3f)) counter_1 (
    .Q(counter_1_q), .clk(divider_1_out[0]));  // open: load, D, count, carry, clr
  Hex_Digit_Display hex_digit_display_1 (.value(divider_2_out));  // open: dp
  Divider #(.width(6)) divider_2 (
    .a(divider_1_rem), .b(in_1), .out({divider_2_out_2, divider_2_out}), .rem(divider_2_rem));  // open: upper
  // Probe on divider_2_out
  // Probe on {divider_2_out_2, divider_2_out}
  Hex_Digit_Display hex_digit_display_2 (.value(divider_2_rem[3:0]));  // open: dp
endmodule
