// Logisim project cpu.circ as structural Verilog: 10 circuits, main circuit total
// ALU
module alu (
  input  [15:0] A,
  input  [15:0] B,
  input  [3:0] OP,
  output EQ,
  output LT,
  output [15:0] RESULT,
  output [15:0] HI
);

  wire [15:0] adder_1_out, and_1_out, divider_1_out, divider_1_rem, multiplier_1_cout, multiplier_1_out,
       nor_1_out, or_1_out, shifter_1_out, shifter_2_out, shifter_3_out, subtractor_1_out, xor_1_out;

  Comparator #(.width(16)) comparator_1 (.a(A), .b(B), .eq(EQ), .lt(LT));  // open: gt
  Adder #(.width(16)) adder_1 (.a(A), .b(B), .out(adder_1_out));  // open: cin, cout
  Subtractor #(.width(16)) subtractor_1 (.a(A), .b(B), .out(subtractor_1_out));  // open: bin, bout
  Shifter #(.width(16)) shifter_1 (.in(A), .\dist (B[3:0]), .out(shifter_1_out));
  Shifter #(.width(16), .shift("lr")) shifter_2 (.in(A), .\dist (B[3:0]), .out(shifter_2_out));
  Shifter #(.width(16), .shift("ar")) shifter_3 (.in(A), .\dist (B[3:0]), .out(shifter_3_out));
  assign and_1_out = A & B;  // AND_Gate and_1, 16 bits wide
  assign or_1_out = A | B;  // OR_Gate or_1, 16 bits wide
  assign nor_1_out = ~(A | B);  // NOR_Gate nor_1, 16 bits wide
  assign xor_1_out = A ^ B;  // XOR_Gate xor_1, 16 bits wide
  Multiplier #(.width(16)) multiplier_1 (.a(A), .b(B), .out(multiplier_1_out), .cout(multiplier_1_cout));  // open: cin
  Divider #(.width(16)) divider_1 (.a(A), .b(B), .out(divider_1_out), .rem(divider_1_rem));  // open: upper
  Multiplexer #(.select(4), .width(16), .enable("false")) multiplexer_1 (
    .in0(adder_1_out), .in1(subtractor_1_out), .in2(shifter_1_out), .in3(shifter_2_out), .in4(shifter_3_out),
    .in5(and_1_out), .in6(or_1_out), .in7(nor_1_out), .in8(xor_1_out), .in9(multiplier_1_out),
    .in10(divider_1_out), .out(RESULT), .sel(OP));  // open: in11, in12, in13, in14, in15
  Multiplexer #(.select(4), .width(16), .enable("false")) multiplexer_2 (
    .in9(multiplier_1_cout), .in10(divider_1_rem), .out(HI), .sel(OP));  // open: in0, in1, in2, in3, in4, in5, in6, in7, in8, in11, in12, in13, in14, in15
  Pull_Resistor pull_resistor_1 (.node(RESULT));
  Pull_Resistor pull_resistor_2 (.node(HI));
endmodule

// CPU
module cpu (
  input  CLOCK_IN,
  input  RESET,
  input  [15:0] DATA_IN,
  output MEM_WRT,
  output [15:0] DATA_OUT,
  output [15:0] ADDRESS,
  output HALT
);

  wire alu_1_eq, alu_1_lt, controlled_buffer_1_out, d_ff_1_q, FETCH_q, gate_control_1_alu_b_src,
       gate_control_1_fetch_2, gate_control_1_hi_wrt, gate_control_1_ir_wrt, gate_control_1_lo_wrt,
       gate_control_1_mar_src, gate_control_1_op_wrt, gate_control_1_reg_src2_src, gate_control_1_reg_wrt,
       gate_control_1_result_wrt, gate_control_1_t_reset, multiplexer_2_out, not_1_out, not_2_out, not_3_out,
       or_1_out;
  wire [1:0] gate_control_1_pc_src, gate_control_1_pc_wrt;
  wire [2:0] gate_control_1_reg_src;
  wire [3:0] gate_control_1_alu_op, IR_q, IR_q_2, multiplexer_6_out, T_q;
  wire [7:0] IR_q_3;
  wire [11:0] OP_q;
  wire [15:0] adder_1_out, adder_2_out, alu_1_hi, alu_1_result, bit_extender_1_out, HI_q, LO_q,
       multiplexer_1_out, multiplexer_4_out, multiplexer_5_out, PC_q, reg_1_src1_out, RESULT_q, shifter_1_out;
  wire [15:12] OP_q_2;

  Shifter #(.width(16)) shifter_1 (.in({OP_q_2, OP_q}), .\dist (4'b0001), .out(shifter_1_out));
  not not_1 (not_1_out, alu_1_eq);
  assign controlled_buffer_1_out = not_2_out ? CLOCK_IN : 1'bz;  // Controlled_Buffer controlled_buffer_1
  not not_2 (not_2_out, HALT);
  Adder #(.width(16)) adder_1 (.a(PC_q), .b(shifter_1_out), .out(adder_1_out));  // open: cin, cout
  Adder #(.width(16)) adder_2 (.a(PC_q), .b(16'h1), .out(adder_2_out));  // open: cin, cout
  not not_3 (not_3_out, controlled_buffer_1_out);
  // Probe on adder_1_out
  Multiplexer #(.select(2), .width(16), .enable("false")) multiplexer_1 (
    .in0(adder_2_out), .in1(adder_1_out), .in2({OP_q_2, OP_q}), .in3(DATA_OUT), .out(multiplexer_1_out),
    .sel(gate_control_1_pc_src));
  Counter #(.width(4), .max('hf)) T (.Q(T_q), .clk(not_3_out), .clr(or_1_out));  // open: load, D, count, carry
  Register #(.width(16)) PC (
    .D(multiplexer_1_out), .en(multiplexer_2_out), .Q(PC_q), .clk(controlled_buffer_1_out), .clr(RESET));
  Multiplexer #(.select(2), .enable("false")) multiplexer_2 (
    .in0(1'b0), .in1(1'b1), .in2(alu_1_eq), .in3(not_1_out), .out(multiplexer_2_out),
    .sel(gate_control_1_pc_wrt));
  D_Flip_Flop FETCH (.clk(not_3_out), .D(gate_control_1_fetch_2), .Q(FETCH_q), .preset(RESET));  // open: Qn, en, reset
  or or_1 (or_1_out, d_ff_1_q, RESET);
  D_Flip_Flop d_ff_1 (.clk(not_3_out), .D(gate_control_1_t_reset), .Q(d_ff_1_q));  // open: Qn, preset, en, reset
  gate_control gate_control_1 (
    .HALT(HALT), .T_RESET(gate_control_1_t_reset), .FETCH_2(gate_control_1_fetch_2),
    .PC_SRC(gate_control_1_pc_src), .PC_WRT(gate_control_1_pc_wrt), .MAR_SRC(gate_control_1_mar_src),
    .MEM_WRT(MEM_WRT), .IR_WRT(gate_control_1_ir_wrt), .OP_WRT(gate_control_1_op_wrt),
    .REG_SRC(gate_control_1_reg_src), .REG_WRT(gate_control_1_reg_wrt), .ALU_B_SRC(gate_control_1_alu_b_src),
    .REG_SRC2_SRC(gate_control_1_reg_src2_src), .ALU_OP(gate_control_1_alu_op),
    .RESULT_WRT(gate_control_1_result_wrt), .LO_WRT(gate_control_1_lo_wrt), .HI_WRT(gate_control_1_hi_wrt),
    .INSTRUCTION(IR_q_3[4:0]), .T(T_q), .FETCH(FETCH_q));
  Register #(.width(16)) IR (
    .D(DATA_IN), .en(gate_control_1_ir_wrt), .Q({IR_q_3, IR_q_2, IR_q}), .clk(controlled_buffer_1_out));  // open: clr
  Multiplexer #(.width(16), .enable("false")) multiplexer_3 (
    .in0(PC_q), .in1(RESULT_q), .out(ADDRESS), .sel(gate_control_1_mar_src));
  // Probe on DATA_IN
  Multiplexer #(.select(3), .width(16), .enable("false")) multiplexer_4 (
    .in0(RESULT_q), .in1(bit_extender_1_out), .in2(PC_q), .in3(HI_q), .in4(LO_q), .in5(DATA_IN),
    .out(multiplexer_4_out), .sel(gate_control_1_reg_src));  // open: in6, in7
  Register #(.width(16)) OP (
    .D(DATA_IN), .en(gate_control_1_op_wrt), .Q({OP_q_2, OP_q}), .clk(controlled_buffer_1_out));  // open: clr
  \reg  reg_1 (
    .SRC1_REG(IR_q), .SRC2_REG(multiplexer_6_out), .CLOCK(controlled_buffer_1_out),
    .WRITE(gate_control_1_reg_wrt), .DATA_IN(multiplexer_4_out), .DST_REG(IR_q_2), .SRC1_OUT(reg_1_src1_out),
    .SRC2_OUT(DATA_OUT));
  Multiplexer #(.width(16), .enable("false")) multiplexer_5 (
    .in0(DATA_OUT), .in1({OP_q_2, OP_q}), .out(multiplexer_5_out), .sel(gate_control_1_alu_b_src));
  Multiplexer #(.width(4), .enable("false")) multiplexer_6 (
    .in0(OP_q_2), .in1(IR_q_2), .out(multiplexer_6_out), .sel(gate_control_1_reg_src2_src));
  alu alu_1 (
    .A(reg_1_src1_out), .B(multiplexer_5_out), .OP(gate_control_1_alu_op), .EQ(alu_1_eq), .LT(alu_1_lt),
    .RESULT(alu_1_result), .HI(alu_1_hi));
  Register #(.width(16)) LO (
    .D(alu_1_result), .en(gate_control_1_lo_wrt), .Q(LO_q), .clk(controlled_buffer_1_out));  // open: clr
  assign bit_extender_1_out = {{15{1'b0}}, alu_1_lt};  // Bit_Extender bit_extender_1
  Register #(.width(16)) HI (
    .D(alu_1_hi), .en(gate_control_1_hi_wrt), .Q(HI_q), .clk(controlled_buffer_1_out));  // open: clr
  Register #(.width(16)) RESULT (
    .D(alu_1_result), .en(gate_control_1_result_wrt), .Q(RESULT_q), .clk(controlled_buffer_1_out));  // open: clr
endmodule

// REG
module \reg  (
  input  [3:0] SRC1_REG,
  input  [3:0] SRC2_REG,
  input  CLOCK,
  input  WRITE,
  input  [15:0] DATA_IN,
  input  [3:0] DST_REG,
  output [15:0] SRC1_OUT,
  output [15:0] SRC2_OUT
);

  wire and_1_out, and_2_out, and_3_out, and_4_out, and_5_out, and_6_out, and_7_out, and_8_out, and_9_out,
       and_10_out, and_11_out, and_12_out, and_13_out, and_14_out, and_15_out, decoder_1_out1,
       decoder_1_out2, decoder_1_out3, decoder_1_out4, decoder_1_out5, decoder_1_out6, decoder_1_out7,
       decoder_1_out8, decoder_1_out9, decoder_1_out10, decoder_1_out11, decoder_1_out12, decoder_1_out13,
       decoder_1_out14, decoder_1_out15, decoder_2_out0, decoder_2_out1, decoder_2_out2, decoder_2_out3,
       decoder_2_out4, decoder_2_out5, decoder_2_out6, decoder_2_out7, decoder_2_out8, decoder_2_out9,
       decoder_2_out10, decoder_2_out11, decoder_2_out12, decoder_2_out13, decoder_2_out14, decoder_2_out15,
       decoder_3_out0, decoder_3_out1, decoder_3_out2, decoder_3_out3, decoder_3_out4, decoder_3_out5,
       decoder_3_out6, decoder_3_out7, decoder_3_out8, decoder_3_out9, decoder_3_out10, decoder_3_out11,
       decoder_3_out12, decoder_3_out13, decoder_3_out14, decoder_3_out15;
  wire [15:0] R1_q, R2_q, R3_q, R4_q, R5_q, R6_q, R7_q, R8_q, R9_q, R10_q, R11_q, R12_q, R13_q, R14_q, R15_q;

  Decoder #(.select(4), .enable("false")) decoder_1 (
    .out1(decoder_1_out1), .out2(decoder_1_out2), .out3(decoder_1_out3), .out4(decoder_1_out4),
    .out5(decoder_1_out5), .out6(decoder_1_out6), .out7(decoder_1_out7), .out8(decoder_1_out8),
    .out9(decoder_1_out9), .out10(decoder_1_out10), .out11(decoder_1_out11), .out12(decoder_1_out12),
    .out13(decoder_1_out13), .out14(decoder_1_out14), .out15(decoder_1_out15), .sel(DST_REG));  // open: out0
  and and_1 (and_1_out, decoder_1_out1, WRITE);
  and and_2 (and_2_out, decoder_1_out2, WRITE);
  and and_3 (and_3_out, decoder_1_out3, WRITE);
  and and_4 (and_4_out, decoder_1_out4, WRITE);
  and and_5 (and_5_out, decoder_1_out5, WRITE);
  and and_6 (and_6_out, decoder_1_out6, WRITE);
  and and_7 (and_7_out, decoder_1_out7, WRITE);
  and and_8 (and_8_out, decoder_1_out8, WRITE);
  and and_9 (and_9_out, decoder_1_out9, WRITE);
  and and_10 (and_10_out, decoder_1_out10, WRITE);
  and and_11 (and_11_out, decoder_1_out11, WRITE);
  and and_12 (and_12_out, decoder_1_out12, WRITE);
  and and_13 (and_13_out, decoder_1_out13, WRITE);
  and and_14 (and_14_out, decoder_1_out14, WRITE);
  and and_15 (and_15_out, decoder_1_out15, WRITE);
  Register #(.width(16)) R1 (.D(DATA_IN), .en(and_1_out), .Q(R1_q), .clk(CLOCK));  // open: clr
  Register #(.width(16)) R2 (.D(DATA_IN), .en(and_2_out), .Q(R2_q), .clk(CLOCK));  // open: clr
  Register #(.width(16)) R3 (.D(DATA_IN), .en(and_3_out), .Q(R3_q), .clk(CLOCK));  // open: clr
  Register #(.width(16)) R4 (.D(DATA_IN), .en(and_4_out), .Q(R4_q), .clk(CLOCK));  // open: clr
  Register #(.width(16)) R5 (.D(DATA_IN), .en(and_5_out), .Q(R5_q), .clk(CLOCK));  // open: clr
  Register #(.width(16)) R6 (.D(DATA_IN), .en(and_6_out), .Q(R6_q), .clk(CLOCK));  // open: clr
  Register #(.width(16)) R7 (.D(DATA_IN), .en(and_7_out), .Q(R7_q), .clk(CLOCK));  // open: clr
  Register #(.width(16)) R8 (.D(DATA_IN), .en(and_8_out), .Q(R8_q), .clk(CLOCK));  // open: clr
  Register #(.width(16)) R9 (.D(DATA_IN), .en(and_9_out), .Q(R9_q), .clk(CLOCK));  // open: clr
  Register #(.width(16)) R10 (.D(DATA_IN), .en(and_10_out), .Q(R10_q), .clk(CLOCK));  // open: clr
  Register #(.width(16)) R11 (.D(DATA_IN), .en(and_11_out), .Q(R11_q), .clk(CLOCK));  // open: clr
  Register #(.width(16)) R12 (.D(DATA_IN), .en(and_12_out), .Q(R12_q), .clk(CLOCK));  // open: clr
  Register #(.width(16)) R13 (.D(DATA_IN), .en(and_13_out), .Q(R13_q), .clk(CLOCK));  // open: clr
  Register #(.width(16)) R14 (.D(DATA_IN), .en(and_14_out), .Q(R14_q), .clk(CLOCK));  // open: clr
  Register #(.width(16)) R15 (.D(DATA_IN), .en(and_15_out), .Q(R15_q), .clk(CLOCK));  // open: clr
  Decoder #(.select(4), .enable("false")) decoder_2 (
    .out0(decoder_2_out0), .out1(decoder_2_out1), .out2(decoder_2_out2), .out3(decoder_2_out3),
    .out4(decoder_2_out4), .out5(decoder_2_out5), .out6(decoder_2_out6), .out7(decoder_2_out7),
    .out8(decoder_2_out8), .out9(decoder_2_out9), .out10(decoder_2_out10), .out11(decoder_2_out11),
    .out12(decoder_2_out12), .out13(decoder_2_out13), .out14(decoder_2_out14), .out15(decoder_2_out15),
    .sel(SRC1_REG));
  assign SRC1_OUT = decoder_2_out0 ? {16{1'b0}} : 16'bz;  // Controlled_Buffer controlled_buffer_1
  assign SRC1_OUT = decoder_2_out1 ? R1_q : 16'bz;  // Controlled_Buffer controlled_buffer_2
  assign SRC1_OUT = decoder_2_out2 ? R2_q : 16'bz;  // Controlled_Buffer controlled_buffer_3
  assign SRC1_OUT = decoder_2_out3 ? R3_q : 16'bz;  // Controlled_Buffer controlled_buffer_4
  assign SRC1_OUT = decoder_2_out4 ? R4_q : 16'bz;  // Controlled_Buffer controlled_buffer_5
  assign SRC1_OUT = decoder_2_out5 ? R5_q : 16'bz;  // Controlled_Buffer controlled_buffer_6
  assign SRC1_OUT = decoder_2_out6 ? R6_q : 16'bz;  // Controlled_Buffer controlled_buffer_7
  assign SRC1_OUT = decoder_2_out7 ? R7_q : 16'bz;  // Controlled_Buffer controlled_buffer_8
  assign SRC1_OUT = decoder_2_out8 ? R8_q : 16'bz;  // Controlled_Buffer controlled_buffer_9
  assign SRC1_OUT = decoder_2_out9 ? R9_q : 16'bz;  // Controlled_Buffer controlled_buffer_10
  assign SRC1_OUT = decoder_2_out10 ? R10_q : 16'bz;  // Controlled_Buffer controlled_buffer_11
  assign SRC1_OUT = decoder_2_out11 ? R11_q : 16'bz;  // Controlled_Buffer controlled_buffer_12
  assign SRC1_OUT = decoder_2_out12 ? R12_q : 16'bz;  // Controlled_Buffer controlled_buffer_13
  assign SRC1_OUT = decoder_2_out13 ? R13_q : 16'bz;  // Controlled_Buffer controlled_buffer_14
  assign SRC1_OUT = decoder_2_out14 ? R14_q : 16'bz;  // Controlled_Buffer controlled_buffer_15
  assign SRC1_OUT = decoder_2_out15 ? R15_q : 16'bz;  // Controlled_Buffer controlled_buffer_16
  Decoder #(.select(4), .enable("false")) decoder_3 (
    .out0(decoder_3_out0), .out1(decoder_3_out1), .out2(decoder_3_out2), .out3(decoder_3_out3),
    .out4(decoder_3_out4), .out5(decoder_3_out5), .out6(decoder_3_out6), .out7(decoder_3_out7),
    .out8(decoder_3_out8), .out9(decoder_3_out9), .out10(decoder_3_out10), .out11(decoder_3_out11),
    .out12(decoder_3_out12), .out13(decoder_3_out13), .out14(decoder_3_out14), .out15(decoder_3_out15),
    .sel(SRC2_REG));
  assign SRC2_OUT = decoder_3_out0 ? {16{1'b0}} : 16'bz;  // Controlled_Buffer controlled_buffer_17
  assign SRC2_OUT = decoder_3_out1 ? R1_q : 16'bz;  // Controlled_Buffer controlled_buffer_18
  assign SRC2_OUT = decoder_3_out2 ? R2_q : 16'bz;  // Controlled_Buffer controlled_buffer_19
  assign SRC2_OUT = decoder_3_out3 ? R3_q : 16'bz;  // Controlled_Buffer controlled_buffer_20
  assign SRC2_OUT = decoder_3_out4 ? R4_q : 16'bz;  // Controlled_Buffer controlled_buffer_21
  assign SRC2_OUT = decoder_3_out5 ? R5_q : 16'bz;  // Controlled_Buffer controlled_buffer_22
  assign SRC2_OUT = decoder_3_out6 ? R6_q : 16'bz;  // Controlled_Buffer controlled_buffer_23
  assign SRC2_OUT = decoder_3_out7 ? R7_q : 16'bz;  // Controlled_Buffer controlled_buffer_24
  assign SRC2_OUT = decoder_3_out8 ? R8_q : 16'bz;  // Controlled_Buffer controlled_buffer_25
  assign SRC2_OUT = decoder_3_out9 ? R9_q : 16'bz;  // Controlled_Buffer controlled_buffer_26
  assign SRC2_OUT = decoder_3_out10 ? R10_q : 16'bz;  // Controlled_Buffer controlled_buffer_27
  assign SRC2_OUT = decoder_3_out11 ? R11_q : 16'bz;  // Controlled_Buffer controlled_buffer_28
  assign SRC2_OUT = decoder_3_out12 ? R12_q : 16'bz;  // Controlled_Buffer controlled_buffer_29
  assign SRC2_OUT = decoder_3_out13 ? R13_q : 16'bz;  // Controlled_Buffer controlled_buffer_30
  assign SRC2_OUT = decoder_3_out14 ? R14_q : 16'bz;  // Controlled_Buffer controlled_buffer_31
  assign SRC2_OUT = decoder_3_out15 ? R15_q : 16'bz;  // Controlled_Buffer controlled_buffer_32

  // Notes on the sheet:
  //   R0 ZERO
endmodule

// CONTROL
module mc_control (
  input  [4:0] INSTRUCTION,
  input  FETCH,
  input  [3:0] T,
  output HALT,
  output T_RESET,
  output FETCH_2,
  output [1:0] PC_SRC,
  output [1:0] PC_WRT,
  output MAR_SRC,
  output MEM_WRT,
  output IR_WRT,
  output OP_WRT,
  output [2:0] REG_SRC,
  output REG_WRITE,
  output ALU_B_SRC,
  output REG_SRC2_SRC,
  output [3:0] ALU_OP,
  output RESULT_WRT,
  output LO_WRT,
  output HI_WRT
);

  wire [4:0] multiplexer_1_out;

  Multiplexer #(.width(5), .enable("false")) multiplexer_1 (
    .in0(INSTRUCTION), .in1({5{1'b0}}), .out(multiplexer_1_out), .sel(FETCH));
  // Probe on {2'b00, FETCH, multiplexer_1_out, T}
  ROM #(.addrWidth(12), .dataWidth(24)) rom_1 (
    .addr({2'b00, FETCH, multiplexer_1_out, T}),
    .data({HALT, T_RESET, FETCH_2, PC_SRC, PC_WRT, MAR_SRC, MEM_WRT, IR_WRT, OP_WRT, REG_SRC, REG_WRITE, ALU_B_SRC, REG_SRC2_SRC, ALU_OP, RESULT_WRT, LO_WRT, HI_WRT}));  // open: sel

  // Notes on the sheet:
  //   contents of rom_1 (hex, n*v repeats v):
  //   4*800000 4 600200 14*800000 104 600200 14*800000 c 600200 14*800000 60004b 15*800000 600053
  //   15*800000 114 600200 14*800000 11c 600200 14*800000 124 600200 14*800000 14 600200 14*800000 1c
  //   600200 14*800000 24 600200 14*800000 6c0080 15*800000 6e0080 15*800000 600600 15*800000 600700
  //   15*800000 2c 600200 14*800000 12c 600200 14*800000 34 600200 14*800000 134 600200 14*800000 44
  //   600200 14*800000 3c 600200 14*800000 720000 15*800000 7a0000 15*800000 a00 720000 14*800000 a00
  //   7a0000 14*800000 104 611600 14*800000 104 618080 14*800000 600e00 15*800000 601200 59*800000 204000
  //   220000 202000 20000 3580*800000
endmodule

module total (
);

  wire CLOCK_out, comparator_1_eq, comparator_2_eq, comparator_3_eq, comparator_4_eq, comparator_5_eq,
       comparator_6_eq, comparator_7_eq, comparator_8_eq, counter_2_carry, cpu_1_halt, cpu_1_mem_wrt,
       d_ff_1_q, keyboard_1_avail, not_1_out, not_2_out, not_3_out, not_4_out, or_1_out, or_2_out, or_3_out,
       or_4_out, RESET_out;
  wire [6:0] cpu_1_data_out, keyboard_1_data;
  wire [8:0] cpu_1_data_out_2;
  wire [15:0] bit_extender_1_out, bit_extender_2_out, controlled_buffer_1_out, controlled_buffer_3_out,
       controlled_buffer_6_out, counter_1_q, counter_2_q, cpu_1_address, ram_1_data, random_1_out;

  Clock CLOCK (.out(CLOCK_out));
  Button RESET (.out(RESET_out));
  D_Flip_Flop d_ff_1 (.clk(CLOCK_out), .D(counter_2_carry), .Q(d_ff_1_q));  // open: Qn, preset, en, reset
  cpu cpu_1 (
    .CLOCK_IN(CLOCK_out), .DATA_IN(controlled_buffer_1_out), .MEM_WRT(cpu_1_mem_wrt),
    .DATA_OUT({cpu_1_data_out_2, cpu_1_data_out}), .ADDRESS(cpu_1_address), .RESET(RESET_out),
    .HALT(cpu_1_halt));
  Counter #(.width(16), .max('hffff)) counter_1 (
    .Q(counter_1_q), .clk(d_ff_1_q), .clr(RESET_out));  // open: load, D, count, carry
  LED HALT (.in(cpu_1_halt));
  Comparator #(.width(16), .mode("unsigned")) comparator_1 (
    .a(cpu_1_address), .b(16'hf002), .eq(comparator_1_eq));  // open: gt, lt
  Random #(.width(16)) random_1 (.clk(CLOCK_out), .out(random_1_out));  // open: next, clr
  Counter #(.width(16), .max('hffff)) counter_2 (
    .Q(counter_2_q), .carry(counter_2_carry), .clk(CLOCK_out), .clr(RESET_out));  // open: load, D, count
  assign controlled_buffer_1_out = not_1_out ? controlled_buffer_6_out : 16'bz;  // Controlled_Buffer controlled_buffer_1
  assign controlled_buffer_1_out = comparator_1_eq ? random_1_out : 16'bz;  // Controlled_Buffer controlled_buffer_2
  not not_1 (not_1_out, comparator_1_eq);
  Comparator #(.width(16), .mode("unsigned")) comparator_2 (
    .a(cpu_1_address), .b(16'hfffe), .eq(comparator_2_eq));  // open: gt, lt
  Comparator #(.width(16), .mode("unsigned")) comparator_3 (
    .a(cpu_1_address), .b({16{1'b1}}), .eq(comparator_3_eq));  // open: gt, lt
  not not_2 (not_2_out, cpu_1_mem_wrt);
  RAM #(.addrWidth(16), .dataWidth(16), .bus("separate")) ram_1 (
    .addr(cpu_1_address), .din({cpu_1_data_out_2, cpu_1_data_out}), .data(ram_1_data), .str(cpu_1_mem_wrt),
    .clk(CLOCK_out), .ld(not_2_out));  // open: sel, clr
  assign controlled_buffer_3_out = comparator_5_eq ? counter_1_q : 16'bz;  // Controlled_Buffer controlled_buffer_3
  assign controlled_buffer_3_out = comparator_4_eq ? counter_2_q : 16'bz;  // Controlled_Buffer controlled_buffer_4
  Comparator #(.width(16), .mode("unsigned")) comparator_4 (
    .a(cpu_1_address), .b(16'hf000), .eq(comparator_4_eq));  // open: gt, lt
  or or_1 (or_1_out, comparator_4_eq, comparator_5_eq);
  not not_3 (not_3_out, or_1_out);
  assign controlled_buffer_3_out = not_3_out ? ram_1_data : 16'bz;  // Controlled_Buffer controlled_buffer_5
  not not_4 (not_4_out, or_2_out);
  or or_2 (or_2_out, comparator_8_eq, comparator_6_eq);
  assign controlled_buffer_6_out = not_4_out ? controlled_buffer_3_out : 16'bz;  // Controlled_Buffer controlled_buffer_6
  assign controlled_buffer_6_out = comparator_8_eq ? bit_extender_2_out : 16'bz;  // Controlled_Buffer controlled_buffer_7
  TTY tty_1 (.data(cpu_1_data_out), .clk(CLOCK_out), .we(comparator_2_eq), .clr(or_3_out));
  or or_3 (or_3_out, comparator_3_eq, RESET_out);
  Comparator #(.width(16), .mode("unsigned")) comparator_5 (
    .a(cpu_1_address), .b(16'hf001), .eq(comparator_5_eq));  // open: gt, lt
  assign controlled_buffer_6_out = comparator_6_eq ? bit_extender_1_out : 16'bz;  // Controlled_Buffer controlled_buffer_8
  Comparator #(.width(16), .mode("unsigned")) comparator_6 (
    .a(cpu_1_address), .b(16'hfffd), .eq(comparator_6_eq));  // open: gt, lt
  Comparator #(.width(16), .mode("unsigned")) comparator_7 (
    .a(cpu_1_address), .b(16'hfffb), .eq(comparator_7_eq));  // open: gt, lt
  Keyboard keyboard_1 (
    .clk(CLOCK_out), .re(comparator_6_eq), .clr(or_4_out), .avail(keyboard_1_avail), .data(keyboard_1_data));
  or or_4 (or_4_out, comparator_7_eq, RESET_out);
  Comparator #(.width(16), .mode("unsigned")) comparator_8 (
    .a(cpu_1_address), .b(16'hfffc), .eq(comparator_8_eq));  // open: gt, lt
  assign bit_extender_1_out = {{9{1'b0}}, keyboard_1_data};  // Bit_Extender bit_extender_1
  assign bit_extender_2_out = {{15{1'b0}}, keyboard_1_avail};  // Bit_Extender bit_extender_2
endmodule

// CONTROL2
module gate_control (
  input  FETCH,
  input  [3:0] T,
  input  [4:0] INSTRUCTION,
  output HALT,
  output T_RESET,
  output FETCH_2,
  output [1:0] PC_SRC,
  output [1:0] PC_WRT,
  output MAR_SRC,
  output MEM_WRT,
  output IR_WRT,
  output OP_WRT,
  output [2:0] REG_SRC,
  output REG_WRT,
  output ALU_B_SRC,
  output REG_SRC2_SRC,
  output [3:0] ALU_OP,
  output RESULT_WRT,
  output LO_WRT,
  output HI_WRT
);

  wire add_2_out, add_out, addi_2_out, addi_out, and_2_out, and_3_out, and_5_out, and_6_out, andi_2_out,
       andi_out, beq_out, bne_out, decoder_1_out0, decoder_1_out1, decoder_1_out2, decoder_1_out3,
       decoder_1_out4, decoder_1_out5, decoder_2_out0, decoder_2_out1, decoder_2_out2, decoder_2_out3,
       decoder_2_out4, decoder_2_out5, decoder_2_out6, decoder_2_out7, decoder_2_out8, decoder_2_out9,
       decoder_2_out10, decoder_2_out11, decoder_2_out12, decoder_2_out13, decoder_2_out14, decoder_2_out15,
       decoder_2_out16, decoder_2_out17, decoder_2_out18, decoder_2_out19, decoder_2_out20, decoder_2_out21,
       decoder_2_out22, decoder_2_out23, decoder_2_out24, decoder_2_out25, decoder_2_out26, decoder_2_out27,
       decoder_2_out28, decoder_2_out31, div_out, j_out, jal_2_out, jal_out, jalr_2_out, jalr_out, jr_out,
       lw_2_out, lw_out, mfhi_out, mflo_out, mul_out, nor_2_out, nor_out, not_1_out, or_2_out, or_3_out,
       or_4_out, or_5_out, or_6_out, or_7_out, or_17_out, or_18_out, or_19_out, or_20_out, or_21_out,
       or_22_out, or_out, ori_2_out, ori_out, sarv_2_out, sarv_out, sll_2_out, sll_out, sllv_2_out, sllv_out,
       slt_out, slti_out, sra_2_out, sra_out, srl_2_out, srl_out, srlv_2_out, srlv_out, sub_2_out, sub_out,
       sw_out, xor_2_out, xor_out;

  not not_1 (not_1_out, FETCH);
  Decoder #(.select(4), .enable("false")) decoder_1 (
    .out0(decoder_1_out0), .out1(decoder_1_out1), .out2(decoder_1_out2), .out3(decoder_1_out3),
    .out4(decoder_1_out4), .out5(decoder_1_out5), .sel(T));  // open: out6, out7, out8, out9, out10, out11, out12, out13, out14, out15
  and and_1 (IR_WRT, FETCH, decoder_1_out0);
  and and_2 (and_2_out, FETCH, decoder_1_out1);
  Decoder #(.select(5)) decoder_2 (
    .out0(decoder_2_out0), .out1(decoder_2_out1), .out2(decoder_2_out2), .out3(decoder_2_out3),
    .out4(decoder_2_out4), .out5(decoder_2_out5), .out6(decoder_2_out6), .out7(decoder_2_out7),
    .out8(decoder_2_out8), .out9(decoder_2_out9), .out10(decoder_2_out10), .out11(decoder_2_out11),
    .out12(decoder_2_out12), .out13(decoder_2_out13), .out14(decoder_2_out14), .out15(decoder_2_out15),
    .out16(decoder_2_out16), .out17(decoder_2_out17), .out18(decoder_2_out18), .out19(decoder_2_out19),
    .out20(decoder_2_out20), .out21(decoder_2_out21), .out22(decoder_2_out22), .out23(decoder_2_out23),
    .out24(decoder_2_out24), .out25(decoder_2_out25), .out26(decoder_2_out26), .out27(decoder_2_out27),
    .out28(decoder_2_out28), .out31(decoder_2_out31), .sel(INSTRUCTION));  // open: out29, out30, en
  and and_3 (and_3_out, FETCH, decoder_1_out3);
  and and_4 (OP_WRT, FETCH, decoder_1_out2);
  and add (add_out, decoder_1_out4, not_1_out, decoder_2_out0);
  and add_2 (add_2_out, decoder_1_out5, not_1_out, decoder_2_out0);
  and addi (addi_out, decoder_1_out4, not_1_out, decoder_2_out1);
  and addi_2 (addi_2_out, decoder_1_out5, not_1_out, decoder_2_out1);
  and sub (sub_out, decoder_1_out4, not_1_out, decoder_2_out2);
  and sub_2 (sub_2_out, decoder_1_out5, not_1_out, decoder_2_out2);
  and div (div_out, decoder_1_out4, not_1_out, decoder_2_out4);
  and mul (mul_out, decoder_1_out4, not_1_out, decoder_2_out3);
  and sll (sll_out, decoder_1_out4, not_1_out, decoder_2_out5);
  and sll_2 (sll_2_out, decoder_1_out5, not_1_out, decoder_2_out5);
  and srl (srl_out, decoder_1_out4, not_1_out, decoder_2_out6);
  and srl_2 (srl_2_out, decoder_1_out5, not_1_out, decoder_2_out6);
  and sra (sra_out, decoder_1_out4, not_1_out, decoder_2_out7);
  and sra_2 (sra_2_out, decoder_1_out5, not_1_out, decoder_2_out7);
  and sllv (sllv_out, decoder_1_out5, not_1_out, decoder_2_out8);
  and sllv_2 (sllv_2_out, decoder_1_out4, not_1_out, decoder_2_out8);
  and srlv (srlv_out, decoder_1_out4, not_1_out, decoder_2_out9);
  and srlv_2 (srlv_2_out, decoder_1_out5, not_1_out, decoder_2_out9);
  and sarv (sarv_out, decoder_1_out4, not_1_out, decoder_2_out10);
  and sarv_2 (sarv_2_out, decoder_1_out5, not_1_out, decoder_2_out10);
  and beq (beq_out, decoder_1_out4, not_1_out, decoder_2_out11);
  and bne (bne_out, decoder_1_out4, not_1_out, decoder_2_out12);
  and slti (slti_out, decoder_1_out4, not_1_out, decoder_2_out14);
  and slt (slt_out, decoder_1_out4, not_1_out, decoder_2_out13);
  and and_5 (and_5_out, decoder_1_out4, not_1_out, decoder_2_out15);
  and and_6 (and_6_out, decoder_1_out5, not_1_out, decoder_2_out15);
  and andi (andi_out, decoder_1_out4, not_1_out, decoder_2_out16);
  and andi_2 (andi_2_out, decoder_1_out5, not_1_out, decoder_2_out16);
  and \or  (or_out, decoder_1_out4, not_1_out, decoder_2_out17);
  and or_2 (or_2_out, decoder_1_out5, not_1_out, decoder_2_out17);
  and ori (ori_out, decoder_1_out5, not_1_out, decoder_2_out18);
  and ori_2 (ori_2_out, decoder_1_out4, not_1_out, decoder_2_out18);
  and \xor  (xor_out, decoder_1_out4, not_1_out, decoder_2_out19);
  and xor_2 (xor_2_out, decoder_1_out5, not_1_out, decoder_2_out19);
  and \nor  (nor_out, decoder_1_out4, not_1_out, decoder_2_out20);
  and nor_2 (nor_2_out, decoder_1_out5, not_1_out, decoder_2_out20);
  and j (j_out, decoder_1_out4, not_1_out, decoder_2_out21);
  and jr (jr_out, decoder_1_out4, not_1_out, decoder_2_out22);
  and jal (jal_out, decoder_1_out5, not_1_out, decoder_2_out23);
  and jal_2 (jal_2_out, decoder_1_out4, not_1_out, decoder_2_out23);
  and jalr (jalr_out, decoder_1_out4, not_1_out, decoder_2_out24);
  and jalr_2 (jalr_2_out, decoder_1_out5, not_1_out, decoder_2_out24);
  and lw (lw_out, decoder_1_out4, not_1_out, decoder_2_out25);
  and lw_2 (lw_2_out, decoder_1_out5, not_1_out, decoder_2_out25);
  and sw (sw_out, decoder_1_out4, not_1_out, decoder_2_out26);
  and sw_2 (MEM_WRT, decoder_1_out5, not_1_out, decoder_2_out26);
  and mflo (mflo_out, decoder_1_out4, not_1_out, decoder_2_out28);
  and mfhi (mfhi_out, decoder_1_out4, not_1_out, decoder_2_out27);
  and u_halt (HALT, decoder_1_out4, not_1_out, decoder_2_out31);
  assign ALU_OP = sub_out ? 4'b0001 : 4'bz;  // Controlled_Buffer controlled_buffer_1
  or or_3 (or_3_out, sll_out, sllv_2_out);
  or or_4 (or_4_out, srl_out, srlv_out);
  or or_5 (or_5_out, sra_out, sarv_out);
  or or_6 (or_6_out, and_5_out, andi_out);
  or or_7 (or_7_out, or_out, ori_2_out);
  Pull_Resistor pull_resistor_1 (.node(ALU_OP));
  or or_8 (MAR_SRC, lw_2_out, MEM_WRT);
  or or_9 (REG_SRC2_SRC, beq_out, bne_out, MEM_WRT);
  or or_10 (HI_WRT, mul_out, div_out);
  or or_11 (LO_WRT, mul_out, div_out);
  or or_12 (T_RESET, add_2_out, addi_2_out, sub_2_out, mul_out, div_out, sll_2_out, srl_2_out, sra_2_out, sllv_out, srlv_2_out, sarv_2_out, beq_out, bne_out, slt_out, slti_out, and_6_out, andi_2_out, or_2_out, ori_out, xor_2_out, nor_2_out, j_out, jr_out, jal_out, jalr_2_out, lw_2_out, MEM_WRT, mfhi_out, mflo_out);
  or or_13 (FETCH_2, IR_WRT, and_2_out, OP_WRT, add_2_out, addi_2_out, sub_2_out, mul_out, div_out, sll_2_out, srl_2_out, sra_2_out, sllv_out, srlv_2_out, sarv_2_out, beq_out, bne_out, slt_out, slti_out, and_6_out, andi_2_out, or_2_out, ori_out, xor_2_out, nor_2_out, j_out, jr_out, jal_out, jalr_2_out, lw_2_out, MEM_WRT, mfhi_out, mflo_out);
  or or_14 (RESULT_WRT, add_out, addi_out, sub_out, sll_out, srl_out, sra_out, sllv_2_out, srlv_out, sarv_out, and_5_out, andi_out, or_out, ori_2_out, xor_out, nor_out, lw_out, sw_out);
  or or_15 (REG_WRT, add_2_out, addi_2_out, sub_2_out, sll_2_out, srl_2_out, sra_2_out, sllv_out, srlv_2_out, sarv_2_out, slt_out, slti_out, and_6_out, andi_2_out, or_2_out, ori_out, xor_2_out, nor_2_out, jal_2_out, jalr_out, lw_2_out, mfhi_out, mflo_out);
  or or_16 (ALU_B_SRC, addi_out, sll_out, srl_out, sra_out, slti_out, andi_out, ori_2_out, lw_out, sw_out);
  or or_17 (or_17_out, and_2_out, and_3_out, j_out, jr_out, jal_out, jalr_2_out);
  or or_18 (or_18_out, beq_out, bne_out);
  or or_19 (or_19_out, j_out, jal_out);
  or or_20 (or_20_out, jr_out, jalr_2_out);
  or or_21 (or_21_out, slt_out, slti_out);
  or or_22 (or_22_out, jal_2_out, jalr_out);
  assign ALU_OP = or_3_out ? 4'b0010 : 4'bz;  // Controlled_Buffer controlled_buffer_2
  assign ALU_OP = or_4_out ? 4'b0011 : 4'bz;  // Controlled_Buffer controlled_buffer_3
  assign ALU_OP = or_5_out ? 4'b0100 : 4'bz;  // Controlled_Buffer controlled_buffer_4
  assign PC_WRT = or_17_out ? 2'b01 : 2'bz;  // Controlled_Buffer controlled_buffer_5
  Pull_Resistor pull_resistor_2 (.node(PC_WRT));
  assign PC_SRC = or_18_out ? 2'b01 : 2'bz;  // Controlled_Buffer controlled_buffer_6
  Pull_Resistor pull_resistor_3 (.node(PC_SRC));
  assign REG_SRC = or_21_out ? 3'b001 : 3'bz;  // Controlled_Buffer controlled_buffer_7
  Pull_Resistor pull_resistor_4 (.node(REG_SRC));
  assign ALU_OP = or_6_out ? 4'b0101 : 4'bz;  // Controlled_Buffer controlled_buffer_8
  assign ALU_OP = or_7_out ? 4'b0110 : 4'bz;  // Controlled_Buffer controlled_buffer_9
  assign PC_WRT = beq_out ? 2'b10 : 2'bz;  // Controlled_Buffer controlled_buffer_10
  assign PC_WRT = bne_out ? 2'b11 : 2'bz;  // Controlled_Buffer controlled_buffer_11
  assign PC_SRC = or_19_out ? 2'b10 : 2'bz;  // Controlled_Buffer controlled_buffer_12
  assign PC_SRC = or_20_out ? 2'b11 : 2'bz;  // Controlled_Buffer controlled_buffer_13
  assign REG_SRC = or_22_out ? 3'b010 : 3'bz;  // Controlled_Buffer controlled_buffer_14
  assign REG_SRC = mfhi_out ? 3'b011 : 3'bz;  // Controlled_Buffer controlled_buffer_15
  assign REG_SRC = mflo_out ? 3'b100 : 3'bz;  // Controlled_Buffer controlled_buffer_16
  assign ALU_OP = nor_out ? 4'b0111 : 4'bz;  // Controlled_Buffer controlled_buffer_17
  assign ALU_OP = xor_out ? 4'b1000 : 4'bz;  // Controlled_Buffer controlled_buffer_18
  assign ALU_OP = mul_out ? 4'b1001 : 4'bz;  // Controlled_Buffer controlled_buffer_19
  assign REG_SRC = lw_2_out ? 3'b101 : 3'bz;  // Controlled_Buffer controlled_buffer_20
  assign ALU_OP = div_out ? 4'b1010 : 4'bz;  // Controlled_Buffer controlled_buffer_21

  // Notes on the sheet:
  //   t0
  //   t1
  //   t2
  //   t3
  //   add t4
  //   add t5
  //   addi t4
  //   addi t5
  //   sub t5
  //   sub t4
  //   mul t4
  //   div t4
  //   sll t5
  //   sll t4
  //   srl t4
  //   sra t4
  //   srl t5
  //   sra t5
  //   sllv t4
  //   sllv t5
  //   srlv t4
  //   srlv t5
  //   srav t5
  //   srav t4
  //   bne t4
  //   beq t4
  //   slti t4
  //   slt t4
  //   and t4
  //   and t5
  //   or t4
  //   andi t4
  //   andi t5
  //   or t5
  //   ori t4
  //   ori t5
  //   xor t5
  //   xor t4
  //   nor t4
  //   nor t5
  //   jr t4
  //   j t4
  //   jal t5
  //   jal t4
  //   jalr t4
  //   jalr t5
  //   sw t4
  //   lw t4
  //   lw t5
  //   sw t5
  //   mfhi t4
  //   mflo t4
endmodule

module pipeline (
);

  wire clock_1_out, d_ff_1_q, d_ff_2_q;
  wire [7:0] counter_1_q, ram_1_data, random_1_out, register_1_q;

  Clock clock_1 (.out(clock_1_out));
  Random random_1 (.clk(clock_1_out), .out(random_1_out));  // open: next, clr
  Counter counter_1 (.Q(counter_1_q), .clk(clock_1_out));  // open: load, D, count, carry, clr
  // Probe on counter_1_q
  Register register_1 (.D(counter_1_q), .Q(register_1_q), .clk(clock_1_out));  // open: en, clr
  D_Flip_Flop d_ff_1 (.clk(clock_1_out), .D(counter_1_q[0]), .Q(d_ff_1_q));  // open: Qn, preset, en, reset
  RAM #(.addrWidth(4), .bus("separate")) ram_1 (
    .addr(counter_1_q[3:0]), .din(counter_1_q), .data(ram_1_data), .str(1'b1), .clk(clock_1_out), .ld(1'b1));  // open: sel, clr
  // Probe on ram_1_data
  Register register_2 (.D(register_1_q), .clk(clock_1_out));  // open: en, Q, clr
  D_Flip_Flop d_ff_2 (.clk(clock_1_out), .D(d_ff_1_q), .Q(d_ff_2_q));  // open: Qn, preset, en, reset
  Register register_3 (.D(ram_1_data), .clk(clock_1_out));  // open: en, Q, clr
endmodule

module computer (
);

  wire CLOCK_out, comparator_1_eq, comparator_2_eq, comparator_3_eq, comparator_4_eq, comparator_5_eq,
       counter_1_not_data_ready, cpu_1_halt, cpu_1_mem_wrt, keyboard_3_avail, not_1_out, not_2_out, or_1_out,
       or_2_out, or_3_out, random_1_not_data_ready, RESET_out, undriven_2, undriven_3, undriven_4,
       undriven_5, undriven_7, undriven_8, undriven_9, undriven_10, undriven_11, undriven_12;
  wire [6:0] cpu_1_data_out, keyboard_1_data, keyboard_2_data, keyboard_3_data, undriven, undriven_6;
  wire [8:0] cpu_1_data_out_2;
  wire [15:0] bit_extender_1_out, bit_extender_2_out, controlled_buffer_3_out, counter_1_data_out,
       cpu_1_address, ram_1_data, random_1_data_out;

  Clock CLOCK (.out(CLOCK_out));
  Button RESET (.out(RESET_out));
  TTY #(.rows(16), .cols(64)) tty_1 (.data(undriven), .clk(undriven_2), .we(undriven_3), .clr(undriven_4));
  Keyboard #(.buflen(255)) keyboard_1 (
    .clk(undriven_2), .re(undriven_9), .clr(undriven_5), .data(keyboard_1_data));  // open: avail
  cpu cpu_1 (
    .CLOCK_IN(CLOCK_out), .DATA_IN(random_1_data_out), .MEM_WRT(cpu_1_mem_wrt),
    .DATA_OUT({cpu_1_data_out_2, cpu_1_data_out}), .ADDRESS(cpu_1_address), .RESET(RESET_out),
    .HALT(cpu_1_halt));
  LED HALT (.in(cpu_1_halt));
  TTY #(.rows(16), .cols(64)) tty_2 (.data(undriven_6), .clk(undriven_7), .we(undriven_8), .clr(undriven_11));
  Keyboard #(.buflen(255)) keyboard_2 (
    .clk(undriven_7), .re(undriven_10), .clr(undriven_12), .data(keyboard_2_data));  // open: avail
  random random_1 (
    .ADDRESS_IN(cpu_1_address), .ADDR(16'hf002), .CLOCK(CLOCK_out), .NOT_DATA_READY(random_1_not_data_ready),
    .DATA_OUT(random_1_data_out));
  assign random_1_data_out = random_1_not_data_ready ? controlled_buffer_3_out : 16'bz;  // Controlled_Buffer controlled_buffer_1
  Comparator #(.width(16), .mode("unsigned")) comparator_1 (
    .a(cpu_1_address), .b(16'hfffe), .eq(comparator_1_eq));  // open: gt, lt
  Comparator #(.width(16), .mode("unsigned")) comparator_2 (
    .a(cpu_1_address), .b({16{1'b1}}), .eq(comparator_2_eq));  // open: gt, lt
  not not_1 (not_1_out, cpu_1_mem_wrt);
  counter counter_1 (
    .CLOCK(CLOCK_out), .ADDRESS(cpu_1_address), .RESET(RESET_out), .DATA_OUT(counter_1_data_out),
    .NOT_DATA_READY(counter_1_not_data_ready), .LO_ADDR(16'hf000), .HI_ADDR(16'hf001));
  RAM #(.addrWidth(16), .dataWidth(16), .bus("separate")) ram_1 (
    .addr(cpu_1_address), .din({cpu_1_data_out_2, cpu_1_data_out}), .data(ram_1_data), .str(cpu_1_mem_wrt),
    .clk(CLOCK_out), .ld(not_1_out));  // open: sel, clr
  assign counter_1_data_out = counter_1_not_data_ready ? ram_1_data : 16'bz;  // Controlled_Buffer controlled_buffer_2
  assign controlled_buffer_3_out = not_2_out ? counter_1_data_out : 16'bz;  // Controlled_Buffer controlled_buffer_3
  not not_2 (not_2_out, or_1_out);
  or or_1 (or_1_out, comparator_5_eq, comparator_3_eq);
  assign controlled_buffer_3_out = comparator_5_eq ? bit_extender_2_out : 16'bz;  // Controlled_Buffer controlled_buffer_4
  TTY #(.rows(16), .cols(64)) tty_3 (.data(cpu_1_data_out), .clk(CLOCK_out), .we(comparator_1_eq), .clr(or_2_out));
  or or_2 (or_2_out, comparator_2_eq, RESET_out);
  assign controlled_buffer_3_out = comparator_3_eq ? bit_extender_1_out : 16'bz;  // Controlled_Buffer controlled_buffer_5
  Keyboard keyboard_3 (
    .clk(CLOCK_out), .re(comparator_3_eq), .clr(or_3_out), .avail(keyboard_3_avail), .data(keyboard_3_data));
  Comparator #(.width(16), .mode("unsigned")) comparator_3 (
    .a(cpu_1_address), .b(16'hfffd), .eq(comparator_3_eq));  // open: gt, lt
  Comparator #(.width(16), .mode("unsigned")) comparator_4 (
    .a(cpu_1_address), .b(16'hfffb), .eq(comparator_4_eq));  // open: gt, lt
  or or_3 (or_3_out, comparator_4_eq, RESET_out);
  Comparator #(.width(16), .mode("unsigned")) comparator_5 (
    .a(cpu_1_address), .b(16'hfffc), .eq(comparator_5_eq));  // open: gt, lt
  assign bit_extender_1_out = {{9{1'b0}}, keyboard_3_data};  // Bit_Extender bit_extender_1
  assign bit_extender_2_out = {{15{1'b0}}, keyboard_3_avail};  // Bit_Extender bit_extender_2

  // Notes on the sheet:
  //   Screen
  //   Keyboard
endmodule

// COUNT
module counter (
  input  CLOCK,
  input  [15:0] ADDRESS,
  input  RESET,
  input  [15:0] HI_ADDR,
  input  [15:0] LO_ADDR,
  output [15:0] DATA_OUT,
  output NOT_DATA_READY
);

  wire comparator_1_eq, comparator_2_eq, COUNT_LO_carry, d_ff_1_q;
  wire [15:0] COUNT_HI_q, COUNT_LO_q;

  Counter #(.width(16), .max('hffff)) COUNT_LO (
    .Q(COUNT_LO_q), .carry(COUNT_LO_carry), .clk(CLOCK), .clr(RESET));  // open: load, D, count
  Counter #(.width(16), .max('hffff)) COUNT_HI (
    .Q(COUNT_HI_q), .clk(d_ff_1_q), .clr(RESET));  // open: load, D, count, carry
  D_Flip_Flop d_ff_1 (.clk(CLOCK), .D(COUNT_LO_carry), .Q(d_ff_1_q));  // open: Qn, preset, en, reset
  assign DATA_OUT = comparator_2_eq ? COUNT_LO_q : 16'bz;  // Controlled_Buffer LO
  assign DATA_OUT = comparator_1_eq ? COUNT_HI_q : 16'bz;  // Controlled_Buffer HI
  Comparator #(.width(16), .mode("unsigned")) comparator_1 (
    .a(ADDRESS), .b(HI_ADDR), .eq(comparator_1_eq));  // open: gt, lt
  Comparator #(.width(16), .mode("unsigned")) comparator_2 (
    .a(ADDRESS), .b(LO_ADDR), .eq(comparator_2_eq));  // open: gt, lt
  nor nor_1 (NOT_DATA_READY, comparator_1_eq, comparator_2_eq);
endmodule

// RAND
module random (
  input  [15:0] ADDRESS_IN,
  input  [15:0] ADDR,
  input  CLOCK,
  output NOT_DATA_READY,
  output [15:0] DATA_OUT
);

  wire comparator_1_eq;
  wire [15:0] random_1_out;

  Comparator #(.width(16), .mode("unsigned")) comparator_1 (
    .a(ADDRESS_IN), .b(ADDR), .eq(comparator_1_eq));  // open: gt, lt
  Random #(.width(16)) random_1 (.clk(CLOCK), .out(random_1_out));  // open: next, clr
  assign DATA_OUT = comparator_1_eq ? random_1_out : 16'bz;  // Controlled_Buffer controlled_buffer_1
  not not_1 (NOT_DATA_READY, comparator_1_eq);
endmodule
